# Fritzing sketch Project_v1 (saved by Fritzing 0.9.3b)

parts:
  Composant1 = Arduino Mega 2560 (Rev3)
  L298N1 = L298N DC motor driver
  DC_Mot_Enc1 = DC Motor with two-phase hall-encoder [part_number=VT-E-G25A-06-177E]
  DC_Mot_Enc2 = DC Motor with two-phase hall-encoder [part_number=VT-E-G25A-06-177E]
  M1 = fc-51 [package=THT]
  M2 = fc-51 [package=THT]
  M3 = fc-51 [package=THT]
  M4 = fc-51 [package=THT]
  M5 = fc-51 [package=THT]

nets:
  N1: Composant1.5V, DC_Mot_Enc1.pin4, DC_Mot_Enc2.pin4, M1.pin1, M1.pin3, M2.pin3, M3.pin3, M4.pin3, M5.pin3
  N2: Composant1.GND, DC_Mot_Enc1.pin3, DC_Mot_Enc2.pin3, M1.pin2, M2.pin2, M3.pin2, M4.pin2, M5.pin2
  N3: Composant1.D2_PWM, L298N1.ENA
  N4: Composant1.D3_PWM, L298N1.ENB
  N5: Composant1.D23, M2.pin1
  N6: Composant1.D25, M3.pin1
  N7: Composant1.D27, M4.pin1
  N8: Composant1.D29, M5.pin1
  N9: Composant1.D39, DC_Mot_Enc2.pin6
  N10: Composant1.D41, DC_Mot_Enc2.pin5
  N11: Composant1.D43, DC_Mot_Enc1.pin6
  N12: Composant1.D45, DC_Mot_Enc1.pin5
  N13: Composant1.D47, L298N1.IN1
  N14: Composant1.D49, L298N1.IN2
  N15: Composant1.D51, L298N1.IN3
  N16: Composant1.D53, L298N1.IN4
  N17: L298N1.OUT1, DC_Mot_Enc2.pin1
  N18: L298N1.OUT2, DC_Mot_Enc2.pin2
  N19: L298N1.OUT3, DC_Mot_Enc1.pin1
  N20: L298N1.OUT4, DC_Mot_Enc1.pin2

custom parts:
  L298N DC motor driver: 2x DC motor driver with 78M05 positive voltage regulator (7..35 V) L298N: max 46 V, 2 A Set 5 V Enable jumper to enable 5 V regultor (needed for the L298N) and +5 V output at screw terminal or supply external +5 V at screw terminal Set ENA and/or ENB to +5 V to enable motor permanently or supply ENA and/or ENB with PWM signal IN1 and IN2 set rotation directory for motor A (OUT1/OUT2) IN2 and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
