# Fritzing sketch fritzing_wiring_schematic_v2-0 (saved by Fritzing 0.9.3b)
breadboards: 1

parts:
  Composant1 = Arduino Mega 2560 (Rev3)
  L298N1 = L298N DC motor driver
  DC_Mot_Enc1 = DC Motor with two-phase hall-encoder [part_number=VT-E-G25A-06-177E]
  DC_Mot_Enc2 = DC Motor with two-phase hall-encoder [part_number=VT-E-G25A-06-177E]
  M1 = fc-51 [package=THT]
  M2 = fc-51 [package=THT]
  M3 = fc-51 [package=THT]
  M4 = fc-51 [package=THT]
  M5 = fc-51 [package=THT]
  Part3 = SRF05 Ultrasonic Rangefinder
  U1 = SWITCH_SPDT [package=kps-1290]
  Composant2 = Thumb Joystick
  C1 = Capacitor Polarized [package=cpol-radial-10uf-25v]

nets:
  N1: Composant1.D13_PWM, L298N1.ENB
  N2: Composant1.D12_PWM, L298N1.IN3
  N3: Composant1.D11_PWM, L298N1.IN4
  N4: Composant1.D10_PWM, L298N1.ENA
  N5: Composant1.D9_PWM, L298N1.IN1
  N6: Composant1.D8_PWM, L298N1.IN2
  VCC: Composant1.5V, M1.pin3, M2.pin3, M3.pin3, M4.pin3, M5.pin3, Part3.VCC, U1.O, Composant2.VCC
  GND: Composant1.GND, M1.pin2, M2.pin2, M3.pin2, M4.pin2, M5.pin2, Part3.GND, U1.S, Composant2.GND
  VIN: Composant1.VIN, L298N1.5V
  N7: Composant1.D0_RX0, Composant2.HORZ
  N8: Composant1.D1_TX0, Composant2.VERT
  N9: Composant1.D2_PWM, Part3.Trig
  N10: Composant1.D3_PWM, Part3.Echo
  N11: Composant1.D6_PWM, C1.+
  N12: Composant1.D23, M5.pin1
  N13: Composant1.D25, M4.pin1
  N14: Composant1.D27, M3.pin1
  N15: Composant1.D29, M1.pin1
  N16: Composant1.D31, M2.pin1
  N17: L298N1.OUT1, DC_Mot_Enc2.pin2
  N18: L298N1.OUT2, DC_Mot_Enc2.pin1
  N19: L298N1.OUT3, DC_Mot_Enc1.pin2
  N20: L298N1.OUT4, DC_Mot_Enc1.pin1
  N21: U1.P, C1.-

custom parts:
  L298N DC motor driver: 2x DC motor driver with 78M05 positive voltage regulator (7..35 V) L298N: max 46 V, 2 A Set 5 V Enable jumper to enable 5 V regultor (needed for the L298N) and +5 V output at screw terminal or supply external +5 V at screw terminal Set ENA and/or ENB to +5 V to enable motor permanently or supply ENA and/or ENB with PWM signal IN1 and IN2 set rotation directory for motor A (OUT1/OUT2) IN2 and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
